// Logisim project Decodificador.circ as structural Verilog
module main (
  input  in_1,
  input  in_2,
  input  in_3,
  input  in_4,
  input  in_5,
  input  in_6,
  input  in_7,
  input  in_8,
  input  in_9
);

  decodificador decodificador_1 (.A(in_1), .B(in_2), .C(in_3), .D(in_4));  // open: a_2, b_2, c_2, d_2, e, f, g
  decodificador decodificador_2 (.A(in_5), .B(in_6), .C(in_7), .D(in_8));  // open: a_2, b_2, c_2, d_2, e, f, g
  _7_Segment_Display u_7_segment_display_1 ();  // open: g, f, a, b, e, d, c, dp
  _7_Segment_Display u_7_segment_display_2 ();  // open: g, f, a, b, e, d, c, dp
  CLA cla_1 (
    .in_1(in_5), .in_2(in_1), .in_3(in_6), .in_4(in_2), .in_5(in_7), .in_6(in_3), .in_7(in_8), .in_8(in_4),
    .in_9(in_9));  // open: out_10, out_11, out_12, out_13, out_14
endmodule

module decodificador (
  input  A,
  input  B,
  input  C,
  input  D,
  output a_2,
  output b_2,
  output c_2,
  output d_2,
  output e,
  output f,
  output g
);

  wire and_1_out, and_2_out, and_3_out, and_4_out, and_5_out, and_6_out, and_7_out, and_8_out, and_9_out,
       and_10_out, and_11_out, and_12_out, and_13_out, and_14_out, and_15_out, and_16_out, and_17_out,
       and_18_out, and_19_out, and_20_out, and_21_out, and_22_out, and_23_out, and_24_out, and_25_out,
       and_26_out, and_27_out, and_28_out, and_29_out, and_30_out, and_31_out, not_1_out, not_2_out,
       not_3_out, not_4_out, not_5_out, not_6_out, not_7_out, not_8_out, not_9_out, not_10_out, not_11_out,
       not_12_out, not_13_out, not_14_out, not_15_out, not_16_out, not_17_out, not_18_out, not_19_out,
       not_20_out, not_21_out, not_22_out, not_23_out, not_24_out, not_25_out, not_26_out, not_27_out,
       not_28_out, not_29_out, not_30_out, not_31_out, not_32_out, not_33_out, not_34_out, not_35_out,
       not_36_out, not_37_out, not_38_out, not_39_out;

  not not_1 (not_1_out, A);
  and and_1 (and_1_out, not_1_out, not_2_out);
  not not_2 (not_2_out, C);
  not not_3 (not_3_out, B);
  and and_2 (and_2_out, not_3_out, not_4_out);
  not not_4 (not_4_out, C);
  not not_5 (not_5_out, B);
  and and_3 (and_3_out, not_5_out, not_6_out);
  not not_6 (not_6_out, D);
  not not_7 (not_7_out, C);
  and and_4 (and_4_out, not_7_out, not_8_out);
  not not_8 (not_8_out, D);
  not not_9 (not_9_out, A);
  and and_5 (and_5_out, not_9_out, B, D);
  and and_6 (and_6_out, A, C);
  not not_10 (not_10_out, A);
  and and_7 (and_7_out, not_10_out, not_11_out);
  not not_11 (not_11_out, C);
  not not_12 (not_12_out, A);
  and and_8 (and_8_out, not_12_out, not_13_out);
  not not_13 (not_13_out, D);
  not not_14 (not_14_out, B);
  and and_9 (and_9_out, not_14_out, D);
  not not_15 (not_15_out, B);
  and and_10 (and_10_out, not_15_out, C);
  and and_11 (and_11_out, B, not_16_out, not_17_out);
  not not_16 (not_16_out, C);
  not not_17 (not_17_out, D);
  not not_18 (not_18_out, B);
  not not_19 (not_19_out, A);
  and and_12 (and_12_out, not_19_out, D);
  not not_20 (not_20_out, A);
  and and_13 (and_13_out, not_20_out, C);
  and and_14 (and_14_out, A, not_21_out);
  not not_21 (not_21_out, C);
  not not_22 (not_22_out, A);
  and and_15 (and_15_out, not_22_out, not_23_out);
  not not_23 (not_23_out, C);
  not not_24 (not_24_out, B);
  and and_16 (and_16_out, not_24_out, not_25_out);
  not not_25 (not_25_out, D);
  not not_26 (not_26_out, A);
  and and_17 (and_17_out, not_26_out, B, D);
  not not_27 (not_27_out, C);
  and and_18 (and_18_out, B, not_27_out, D);
  not not_28 (not_28_out, B);
  and and_19 (and_19_out, A, not_28_out, C);
  and and_20 (and_20_out, A, C, not_29_out);
  not not_29 (not_29_out, D);
  not not_30 (not_30_out, B);
  and and_21 (and_21_out, not_30_out, not_31_out);
  not not_31 (not_31_out, D);
  not not_32 (not_32_out, C);
  and and_22 (and_22_out, not_32_out, not_33_out);
  not not_33 (not_33_out, D);
  and and_23 (and_23_out, A, B);
  not not_34 (not_34_out, B);
  and and_24 (and_24_out, not_34_out, not_35_out);
  not not_35 (not_35_out, D);
  and and_25 (and_25_out, B, C);
  and and_26 (and_26_out, A, C);
  and and_27 (and_27_out, A, B);
  not not_36 (not_36_out, C);
  and and_28 (and_28_out, not_36_out, not_37_out);
  not not_37 (not_37_out, D);
  not not_38 (not_38_out, A);
  and and_29 (and_29_out, not_38_out, B);
  and and_30 (and_30_out, B, D);
  not not_39 (not_39_out, B);
  and and_31 (and_31_out, A, not_39_out, C);
  or or_1 (b_2, and_7_out, and_8_out, and_9_out, and_10_out, and_11_out);
  or or_2 (c_2, not_18_out, and_12_out, and_13_out, and_14_out);
  or or_3 (e, and_21_out, and_22_out, and_23_out);
  or or_4 (f, and_24_out, and_25_out, and_26_out, and_27_out);
  or or_5 (g, and_28_out, and_29_out, and_30_out, and_31_out);
  or or_6 (a_2, and_1_out, and_2_out, and_3_out, and_4_out, and_5_out, and_6_out);
  or or_7 (d_2, and_15_out, and_16_out, and_17_out, and_18_out, and_19_out, and_20_out);
  _7_Segment_Display u_7_segment_display_1 (.g(g), .f(f), .a(a_2), .b(b_2), .e(e), .d(d_2), .c(c_2));  // open: dp
endmodule

module CLA (
  input  in_1,
  input  in_2,
  input  in_3,
  input  in_4,
  input  in_5,
  input  in_6,
  input  in_7,
  input  in_8,
  input  in_9,
  output out_10,
  output out_11,
  output out_12,
  output out_13,
  output out_14
);

  wire nand_1_out, nand_2_out, nand_3_out, nand_4_out, nand_5_out, nand_6_out, nand_7_out, nand_8_out,
       nand_9_out, nand_10_out, nand_11_out, nand_12_out, nand_13_out, nand_14_out, nand_15_out, nand_16_out,
       nand_17_out, nand_18_out, nand_19_out, nand_20_out, nand_21_out, nand_22_out, nand_23_out,
       nand_24_out, nand_25_out, nand_26_out, nand_27_out, nand_28_out, nand_29_out, nand_30_out,
       nand_31_out, nand_32_out, nand_33_out, nand_34_out, nor_1_out, nor_2_out, nor_3_out, nor_4_out,
       not_1_out, not_2_out, not_3_out, not_4_out, not_5_out, not_6_out, not_7_out, not_8_out, not_9_out,
       not_10_out, not_11_out, not_12_out, not_13_out, not_15_out, not_16_out, not_17_out, not_18_out,
       not_19_out, not_20_out, not_21_out, not_22_out, not_23_out, not_24_out, not_25_out, not_26_out,
       not_27_out, not_28_out, not_29_out, not_30_out, not_31_out, not_32_out, not_33_out, not_34_out,
       not_35_out;

  not not_1 (not_1_out, in_1);
  not not_2 (not_2_out, in_2);
  not not_3 (not_3_out, in_3);
  not not_4 (not_4_out, in_4);
  not not_5 (not_5_out, in_5);
  not not_6 (not_6_out, in_6);
  not not_7 (not_7_out, in_7);
  not not_8 (not_8_out, in_8);
  not not_9 (not_9_out, in_9);
  nor nor_1 (nor_1_out, not_1_out, not_2_out);
  nand nand_1 (nand_1_out, not_1_out, not_2_out);
  nor nor_2 (nor_2_out, not_3_out, not_4_out);
  nand nand_2 (nand_2_out, not_3_out, not_4_out);
  nor nor_3 (nor_3_out, not_5_out, not_6_out);
  nand nand_3 (nand_3_out, not_5_out, not_6_out);
  nor nor_4 (nor_4_out, not_7_out, not_8_out);
  nand nand_4 (nand_4_out, not_7_out, not_8_out);
  not not_10 (not_10_out, nor_1_out);
  not not_11 (not_11_out, nand_1_out);
  not not_12 (not_12_out, nor_2_out);
  not not_13 (not_13_out, nand_2_out);
  not not_14 (not_12_out, nor_3_out);
  not not_15 (not_15_out, nand_3_out);
  not not_16 (not_16_out, nor_4_out);
  not not_17 (not_17_out, nand_4_out);
  not not_18 (not_18_out, not_11_out);
  not not_19 (not_19_out, not_13_out);
  not not_20 (not_20_out, not_15_out);
  not not_21 (not_21_out, not_17_out);
  not not_22 (not_22_out, not_11_out);
  nand nand_5 (nand_5_out, not_13_out, not_10_out);
  nand nand_6 (nand_6_out, not_15_out, not_10_out, not_12_out);
  nand nand_7 (nand_7_out, not_17_out, not_10_out, not_12_out, not_12_out);
  nand nand_8 (nand_8_out, not_10_out, not_12_out, not_12_out, not_16_out, not_9_out);
  nand nand_9 (nand_9_out, not_10_out, not_18_out);
  not not_23 (not_23_out, not_13_out);
  nand nand_10 (nand_10_out, not_15_out, not_12_out);
  nand nand_11 (nand_11_out, not_17_out, not_12_out, not_12_out);
  nand nand_12 (nand_12_out, not_12_out, not_12_out, not_12_out, not_16_out, not_9_out);
  nand nand_13 (nand_13_out, not_12_out, not_19_out);
  not not_24 (not_24_out, not_15_out);
  not not_25 (not_25_out, not_17_out);
  nand nand_14 (nand_14_out, not_16_out, not_9_out);
  nand nand_15 (nand_15_out, not_16_out, not_21_out);
  nand nand_16 (nand_16_out, not_17_out, not_12_out);
  nand nand_17 (nand_17_out, not_12_out, not_16_out, not_9_out);
  nand nand_18 (nand_18_out, not_12_out, not_20_out);
  nand nand_19 (nand_19_out, not_22_out, nand_5_out, nand_6_out, nand_7_out, nand_8_out);
  nand nand_20 (nand_20_out, not_23_out, nand_10_out, nand_11_out, nand_12_out);
  nand nand_21 (nand_21_out, not_24_out, nand_16_out, nand_17_out);
  nand nand_22 (nand_22_out, not_25_out, nand_14_out);
  not not_26 (not_26_out, nand_19_out);
  not not_27 (not_27_out, nand_9_out);
  not not_28 (not_28_out, nand_20_out);
  not not_29 (not_29_out, nand_13_out);
  not not_30 (not_30_out, nand_21_out);
  not not_31 (not_31_out, nand_18_out);
  not not_32 (not_32_out, nand_22_out);
  not not_33 (not_33_out, nand_15_out);
  not not_34 (not_34_out, not_9_out);
  not not_35 (not_35_out, not_26_out);
  nand nand_23 (nand_23_out, not_27_out, not_28_out);
  nand nand_24 (nand_24_out, nand_9_out, nand_20_out);
  nand nand_25 (nand_25_out, not_29_out, not_30_out);
  nand nand_26 (nand_26_out, nand_13_out, nand_21_out);
  nand nand_27 (nand_27_out, not_31_out, not_32_out);
  nand nand_28 (nand_28_out, nand_18_out, nand_22_out);
  nand nand_29 (nand_29_out, not_33_out, not_34_out);
  nand nand_30 (nand_30_out, nand_15_out, not_9_out);
  not not_36 (out_10, not_35_out);
  nand nand_31 (nand_31_out, nand_23_out, nand_24_out);
  nand nand_32 (nand_32_out, nand_29_out, nand_30_out);
  not not_37 (out_11, nand_31_out);
  not not_38 (out_12, nand_33_out);
  nand nand_33 (nand_33_out, nand_25_out, nand_26_out);
  nand nand_34 (nand_34_out, nand_27_out, nand_28_out);
  not not_39 (out_13, nand_34_out);
  not not_40 (out_14, nand_32_out);
endmodule
